# Fritzing sketch keyboard-schematic (saved by Fritzing 0.9.3b)
breadboards: 1

parts:
  Componente1 = Arduino Nano (Rev3.0) (ICSP)
  R1 = Resistor [tolerance=±5% resistance=220 package=THT]
  R2 = Resistor [tolerance=±5% resistance=220 package=THT]
  R3 = Resistor [tolerance=±5% resistance=220 package=THT]
  R4 = Resistor [tolerance=±5% resistance=220 package=THT]
  R5 = Resistor [tolerance=±5% resistance=220 package=THT]
  R6 = Resistor [tolerance=±5% resistance=220 package=THT]
  part = Resistor [tolerance=±5% resistance=220 package=THT]
  J1 = Piezo Speaker
  S2 = Momentary Switch [package=ksa_sealed_tac_switch]
  S3 = Momentary Switch [package=ksa_sealed_tac_switch]
  S4 = Momentary Switch [package=ksa_sealed_tac_switch]
  S5 = Momentary Switch [package=ksa_sealed_tac_switch]
  S6 = Momentary Switch [package=ksa_sealed_tac_switch]
  Fruta = Momentary Switch [package=ksa_sealed_tac_switch]
  S8 = Momentary Switch [package=ksa_sealed_tac_switch]

nets:
  N1: Componente1.GND, J1.pin1, S2.2, S2.4, S3.2, S3.4, S4.2, S4.4, S5.2, S5.4, S6.2, S6.4, Fruta.2, Fruta.4, S8.2, S8.4
  N2: Componente1.D8, J1.pin2
  N3: Componente1.5V, R1.Pin_1, R2.Pin_1, R3.Pin_1, R4.Pin_1, R5.Pin_1, R6.Pin_1, part.Pin_1
  N4: Componente1.A6, R1.Pin_0, Fruta.3
  N5: Componente1.A5, R2.Pin_0, S6.3
  N6: Componente1.A4, R3.Pin_0, S4.3
  N7: Componente1.A3, R4.Pin_0, S5.3
  N8: Componente1.A2, R5.Pin_0, S3.3
  N9: Componente1.A1, R6.Pin_0, S2.3
  N10: Componente1.A0, part.Pin_0, S8.3

// code stored in the sketch: codigo.ino
#define NOTE_B0  31
#define NOTE_C1  33
#define NOTE_CS1 35
#define NOTE_D1  37
#define NOTE_DS1 39
#define NOTE_E1  41
#define NOTE_F1  44
#define NOTE_FS1 46
#define NOTE_G1  49
#define NOTE_GS1 52
#define NOTE_A1  55
#define NOTE_AS1 58
#define NOTE_B1  62
#define NOTE_C2  65
#define NOTE_CS2 69
#define NOTE_D2  73
#define NOTE_DS2 78
#define NOTE_E2  82
#define NOTE_F2  87
#define NOTE_FS2 93
#define NOTE_G2  98
#define NOTE_GS2 104
#define NOTE_A2  110
#define NOTE_AS2 117
#define NOTE_B2  123
#define NOTE_C3  131
#define NOTE_CS3 139
#define NOTE_D3  147
#define NOTE_DS3 156
#define NOTE_E3  165
#define NOTE_F3  175
#define NOTE_FS3 185
#define NOTE_G3  196
#define NOTE_GS3 208
#define NOTE_A3  220
#define NOTE_AS3 233
#define NOTE_B3  247
#define NOTE_C4  262
#define NOTE_CS4 277
#define NOTE_D4  294
#define NOTE_DS4 311
#define NOTE_E4  330
#define NOTE_F4  349
#define NOTE_FS4 370
#define NOTE_G4  392
#define NOTE_GS4 415
#define NOTE_A4  440
#define NOTE_AS4 466
#define NOTE_B4  494
#define NOTE_C5  523
#define NOTE_CS5 554
#define NOTE_D5  587
#define NOTE_DS5 622
#define NOTE_E5  659
#define NOTE_F5  698
#define NOTE_FS5 740
#define NOTE_G5  784
#define NOTE_GS5 831
#define NOTE_A5  880
#define NOTE_AS5 932
#define NOTE_B5  988
#define NOTE_C6  1047
#define NOTE_CS6 1109
#define NOTE_D6  1175
#define NOTE_DS6 1245
#define NOTE_E6  1319
#define NOTE_F6  1397
#define NOTE_FS6 1480
#define NOTE_G6  1568
#define NOTE_GS6 1661
#define NOTE_A6  1760
#define NOTE_AS6 1865
#define NOTE_B6  1976
#define NOTE_C7  2093
#define NOTE_CS7 2217
#define NOTE_D7  2349
#define NOTE_DS7 2489
#define NOTE_E7  2637
#define NOTE_F7  2794
#define NOTE_FS7 2960
#define NOTE_G7  3136
#define NOTE_GS7 3322
#define NOTE_A7  3520
#define NOTE_AS7 3729
#define NOTE_B7  3951
#define NOTE_C8  4186
#define NOTE_CS8 4435
#define NOTE_D8  4699
#define NOTE_DS8 4978



const int Buzz = 8;


void setup(){
 //Serial.begin(9600);
// Declaro el zumbador
  pinMode(Buzz, OUTPUT);

}

void loop(){
  /*
 Serial.print("Analog 0: ");
 Serial.println(analogRead(0));
 Serial.print("Analog 0: ");
 Serial.println(analogRead(0));
 Serial.print("Analog 0: ");
 Serial.println(analogRead(0));
 Serial.print("Analog 0: ");
 Serial.println(analogRead(0));
 Serial.println(" ");
 
 Serial.print("Analog 1: ");
 Serial.println(analogRead(1));
 Serial.print("Analog 1: ");
 Serial.println(analogRead(1));
 Serial.print("Analog 1: ");
 Serial.println(analogRead(1));
 Serial.print("Analog 1: ");
 Serial.println(analogRead(1));
 Serial.println(" ");
 */


//Teclado
 if( ((analogRead(0)+analogRead(0)+analogRead(0)+analogRead(0))/4) <=1019){
  tone(Buzz, NOTE_C3, 150);    
 }

 if( ((analogRead(1)+analogRead(1)+analogRead(1)+analogRead(1))/4)<= 1019){  
   tone(Buzz, NOTE_D3, 150);
 }

if( ((analogRead(2)+analogRead(2)+analogRead(2)+analogRead(2))/4)<= 1019){  
   tone(Buzz, NOTE_E3, 150);
 }

if( ((analogRead(3)+analogRead(3)+analogRead(3)+analogRead(3))/4)<= 1019){  
   tone(Buzz, NOTE_F3, 150);
 }

if( ((analogRead(4)+analogRead(4)+analogRead(4)+analogRead(4))/4)<= 1019){  
   tone(Buzz, NOTE_G3, 150);
 }

if( ((analogRead(5)+analogRead(5)+analogRead(5)+analogRead(5))/4)<= 1019){  
   tone(Buzz, NOTE_A3, 150);
 }

if( ((analogRead(6)+analogRead(6))/2)<= 1019){  
   tone(Buzz, NOTE_B3, 150);
 }
 
 






}
